// Logisim project ARM Processor.circ as structural Verilog: 6 circuits, main circuit main
module main (
);

  wire CLK, control_unit_1_alusrc, control_unit_1_memtoreg, control_unit_1_memwrite, control_unit_1_move,
       control_unit_1_pcsrc, control_unit_1_regwrite;
  wire [1:0] control_unit_1_immsrc;
  wire [2:0] control_unit_1_out_9, control_unit_1_regsrc;
  wire [3:0] alu_1_aluflagoutput, multiplexer_2_out, multiplexer_3_out;
  wire [23:0] adder_1_out, adder_2_out, multiplexer_1_out, multiplexer_4_out, PC_q;
  wire [31:0] alu_1_result, bit_extender_1_out, extend_1_output, multiplexer_5_out, multiplexer_6_out,
       ram_1_data, Register_File_rd1, Register_File_rd2, rom_1_data, shifter_1_output;
  wire [31:24] multiplexer_4_out_2;

  Multiplexer #(.width(24), .enable("false")) multiplexer_1 (
    .in0(multiplexer_4_out), .in1(adder_1_out), .out(multiplexer_1_out), .sel(control_unit_1_pcsrc));
  Clock clock_1 (.out(CLK));
  Register #(.width(24)) PC (.D(multiplexer_1_out), .Q(PC_q), .clk(CLK));  // open: en, clr
  Adder #(.width(24)) adder_1 (.a(PC_q), .b(24'h1), .out(adder_1_out));  // open: cin, cout
  ROM #(.addrWidth(24), .dataWidth(32)) rom_1 (.addr(PC_q), .data(rom_1_data));  // open: sel
  Adder #(.width(24)) adder_2 (.a(adder_1_out), .b(24'h1), .out(adder_2_out));  // open: cin, cout
  assign bit_extender_1_out = {{8{1'b0}}, adder_2_out};  // Bit_Extender bit_extender_1
  Multiplexer #(.width(4), .enable("false")) multiplexer_2 (
    .in0(rom_1_data[3:0]), .in1(rom_1_data[15:12]), .out(multiplexer_2_out), .sel(control_unit_1_regsrc[0]));
  Multiplexer #(.select(2), .width(4), .enable("false")) multiplexer_3 (
    .in0(rom_1_data[19:16]), .in1(4'b1111), .in2(rom_1_data[3:0]), .out(multiplexer_3_out),
    .sel(control_unit_1_regsrc[2:1]));  // open: in3
  Control_unit control_unit_1 (
    .Opt(rom_1_data[27:26]), .CLK(CLK), .Cond(rom_1_data[31:28]), .Shift(rom_1_data[6:4]),
    .Rd(rom_1_data[15:12]), .Flags(alu_1_aluflagoutput), .Funct(rom_1_data[25:20]),
    .MemtoReg(control_unit_1_memtoreg), .out_9(control_unit_1_out_9), .RegSrc(control_unit_1_regsrc),
    .PCSrc(control_unit_1_pcsrc), .MemWrite(control_unit_1_memwrite), .ALUSrc(control_unit_1_alusrc),
    .RegWrite(control_unit_1_regwrite), .ImmSrc(control_unit_1_immsrc), .Move(control_unit_1_move));
  Register_File Register_File (
    .A1(multiplexer_3_out), .A2(multiplexer_2_out), .A3(rom_1_data[15:12]), .RD1(Register_File_rd1),
    .WE3(control_unit_1_regwrite), .RD2(Register_File_rd2), .WD3({multiplexer_4_out_2, multiplexer_4_out}),
    .R15(bit_extender_1_out), .CLK(CLK));
  Extend extend_1 (.Input(rom_1_data[23:0]), .Output(extend_1_output), .ImmSrc(control_unit_1_immsrc));
  Shifter shifter_1 (
    .Input(Register_File_rd2), .ShiftType(rom_1_data[6:5]), .Shift_Extent(rom_1_data[11:7]),
    .Output(shifter_1_output));
  Multiplexer #(.width(32), .enable("false")) multiplexer_4 (
    .in0(multiplexer_6_out), .in1(multiplexer_5_out), .out({multiplexer_4_out_2, multiplexer_4_out}),
    .sel(control_unit_1_move));
  Multiplexer #(.width(32), .enable("false")) multiplexer_5 (
    .in0(shifter_1_output), .in1(extend_1_output), .out(multiplexer_5_out), .sel(control_unit_1_alusrc));
  ALU alu_1 (
    .ALU_control_signal(control_unit_1_out_9), .B(multiplexer_5_out), .A(Register_File_rd1),
    .Result(alu_1_result), .AlUflagoutput(alu_1_aluflagoutput));
  RAM #(.addrWidth(24), .dataWidth(32), .bus("separate")) ram_1 (
    .addr(alu_1_result[23:0]), .din(Register_File_rd2), .data(ram_1_data), .str(control_unit_1_memwrite),
    .clk(CLK));  // open: sel, ld, clr
  Multiplexer #(.width(32), .enable("false")) multiplexer_6 (
    .in0(alu_1_result), .in1(ram_1_data), .out(multiplexer_6_out), .sel(control_unit_1_memtoreg));

  // Notes on the sheet:
  //   PC+1 or branch
  //   ROM
  //   Adder
  //   contents of rom_1 (hex, n*v repeats v):
  //   e3a01006 e3a02005 e3a04001 e0813002 e1a03083 e0533004 e1814002 e0014002 e1e44000 e7821000 0 e7924000
  //   1afffffc
  //   Adder
  //   bit extender
  //   MOVE
  //   Imm or Reg
  //   RAM
  //   Load or Data Process
endmodule

module Register_File (
  input  [31:0] WD3,
  input  [3:0] A1,
  input  WE3,
  input  [3:0] A3,
  input  CLK,
  input  [3:0] A2,
  input  [31:0] R15,
  output [31:0] RD1,
  output [31:0] RD2
);

  wire demultiplexer_1_out0, demultiplexer_1_out1, demultiplexer_1_out2, demultiplexer_1_out3,
       demultiplexer_1_out4, demultiplexer_1_out5, demultiplexer_1_out6, demultiplexer_1_out7,
       demultiplexer_1_out8, demultiplexer_1_out9, demultiplexer_1_out10, demultiplexer_1_out11,
       demultiplexer_1_out12, demultiplexer_1_out13, demultiplexer_1_out14;
  wire [31:0] R0_q, R1_q, R2_q, R3_q, R4_q, R5_q, R6_q, R7_q, R8_q, R9_q, R10_q, R11_q, R12_q, R13_q, R15_q;

  Demultiplexer #(.select(4), .enable("false")) demultiplexer_1 (
    .out0(demultiplexer_1_out0), .out1(demultiplexer_1_out1), .out2(demultiplexer_1_out2),
    .out3(demultiplexer_1_out3), .out4(demultiplexer_1_out4), .out5(demultiplexer_1_out5),
    .out6(demultiplexer_1_out6), .out7(demultiplexer_1_out7), .out8(demultiplexer_1_out8),
    .out9(demultiplexer_1_out9), .out10(demultiplexer_1_out10), .out11(demultiplexer_1_out11),
    .out12(demultiplexer_1_out12), .out13(demultiplexer_1_out13), .out14(demultiplexer_1_out14), .in(WE3),
    .sel(A3));  // open: out15
  Register #(.width(32)) R0 (.D(WD3), .en(demultiplexer_1_out0), .Q(R0_q), .clk(CLK));  // open: clr
  Register #(.width(32)) R4 (.D(WD3), .en(demultiplexer_1_out4), .Q(R4_q), .clk(CLK));  // open: clr
  Register #(.width(32)) R8 (.D(WD3), .en(demultiplexer_1_out8), .Q(R8_q), .clk(CLK));  // open: clr
  Register #(.width(32)) R12 (.D(WD3), .en(demultiplexer_1_out12), .Q(R12_q), .clk(CLK));  // open: clr
  Register #(.width(32)) R1 (.D(WD3), .en(demultiplexer_1_out1), .Q(R1_q), .clk(CLK));  // open: clr
  Register #(.width(32)) R5 (.D(WD3), .en(demultiplexer_1_out5), .Q(R5_q), .clk(CLK));  // open: clr
  Register #(.width(32)) R9 (.D(WD3), .en(demultiplexer_1_out9), .Q(R9_q), .clk(CLK));  // open: clr
  Register #(.width(32)) R13 (.D(WD3), .en(demultiplexer_1_out13), .Q(R13_q), .clk(CLK));  // open: clr
  Register #(.width(32)) R2 (.D(WD3), .en(demultiplexer_1_out2), .Q(R2_q), .clk(CLK));  // open: clr
  Register #(.width(32)) R6 (.D(WD3), .en(demultiplexer_1_out6), .Q(R6_q), .clk(CLK));  // open: clr
  Register #(.width(32)) R10 (.D(WD3), .en(demultiplexer_1_out10), .Q(R10_q), .clk(CLK));  // open: clr
  Register #(.width(32)) u_R15 (.D(WD3), .en(demultiplexer_1_out14), .Q(R15_q), .clk(CLK));  // open: clr
  Register #(.width(32)) R3 (.D(WD3), .en(demultiplexer_1_out3), .Q(R3_q), .clk(CLK));  // open: clr
  Register #(.width(32)) R7 (.D(WD3), .en(demultiplexer_1_out7), .Q(R7_q), .clk(CLK));  // open: clr
  Register #(.width(32)) R11 (.D(WD3), .en(demultiplexer_1_out11), .Q(R11_q), .clk(CLK));  // open: clr
  Multiplexer #(.select(4), .width(32), .enable("false")) multiplexer_1 (
    .in0(R0_q), .in1(R1_q), .in2(R2_q), .in3(R3_q), .in4(R4_q), .in5(R5_q), .in6(R6_q), .in7(R7_q),
    .in8(R8_q), .in9(R9_q), .in10(R10_q), .in11(R11_q), .in12(R12_q), .in13(R13_q), .in14(R15_q), .in15(R15),
    .out(RD1), .sel(A1));
  Multiplexer #(.select(4), .width(32), .enable("false")) multiplexer_2 (
    .in0(R0_q), .in1(R1_q), .in2(R2_q), .in3(R3_q), .in4(R4_q), .in5(R5_q), .in6(R6_q), .in7(R7_q),
    .in8(R8_q), .in9(R9_q), .in10(R10_q), .in11(R11_q), .in12(R12_q), .in13(R13_q), .in14(R15_q), .in15(R15),
    .out(RD2), .sel(A2));

  // Notes on the sheet:
  //   Write Signal
  //   Register to be written
  //   Program Counter Reg
  //   Write to Register
  //   Demux
  //   REGISTER FILE
  //   First Source Register
  //   Second Source Register
  //   First read port
  //   Second read port
endmodule

module ALU (
  input  [2:0] ALU_control_signal,
  input  [31:0] B,
  input  [31:0] A,
  output [31:0] Result,
  output [3:0] AlUflagoutput
);

  wire adder_1_cout, BIT_31, not_2_out, not_3_out, xor_1_out, xor_2_out;
  wire [30:0] adder_1_out;
  wire [31:0] and_1_out, multiplexer_1_out, negator_1_out, not_1_out, or_1_out, shifter_1_out, shifter_2_out,
       shifter_3_out;

  Multiplexer #(.width(32), .enable("false")) multiplexer_1 (
    .in0(B), .in1(not_1_out), .out(multiplexer_1_out), .sel(ALU_control_signal[0]));
  assign not_1_out = ~B;  // NOT_Gate not_1, 32 bits wide
  not not_2 (not_2_out, ALU_control_signal[1]);
  ExactlyOne xor_1 (.out(xor_1_out), .in0(B[31]), .in1(A[31]), .in2(ALU_control_signal[0]));
  xor xor_2 (xor_2_out, A[31], BIT_31);
  Adder #(.width(32)) adder_1 (
    .a(multiplexer_1_out), .b(A), .out({BIT_31, adder_1_out}), .cin(ALU_control_signal[0]),
    .cout(adder_1_cout));
  assign and_1_out = B & A;  // AND_Gate and_1, 32 bits wide
  assign or_1_out = B | A;  // OR_Gate or_1, 32 bits wide
  Shifter_part #(.width(32)) shifter_1 (.in(A), .\dist (B[4:0]), .out(shifter_1_out));
  Shifter_part #(.width(32), .shift("lr")) shifter_2 (.in(A), .\dist (B[4:0]), .out(shifter_2_out));
  Shifter_part #(.width(32), .shift("ar")) shifter_3 (.in(A), .\dist (B[4:0]), .out(shifter_3_out));
  Negator #(.width(32)) negator_1 (.in(A), .out(negator_1_out));
  not not_3 (not_3_out, xor_1_out);
  and and_2 (AlUflagoutput[0], not_2_out, not_3_out, xor_2_out);
  and and_3 (AlUflagoutput[1], adder_1_cout, not_2_out);
  Multiplexer #(.select(3), .width(32), .enable("false")) multiplexer_2 (
    .in0({BIT_31, adder_1_out}), .in1({BIT_31, adder_1_out}), .in2(and_1_out), .in3(or_1_out),
    .in4(shifter_1_out), .in5(shifter_2_out), .in6(shifter_3_out), .in7(negator_1_out),
    .out({AlUflagoutput[3], Result[30:0]}), .sel(ALU_control_signal));
  Comparator #(.width(32)) comparator_1 (
    .a({AlUflagoutput[3], Result[30:0]}), .b({32{1'b0}}), .eq(AlUflagoutput[2]));  // open: gt, lt

  assign Result[31] = AlUflagoutput[3];

  // Notes on the sheet:
  //   Overflow
  //   last bit
  //   Comparator
  //   Flags Description
  //   3. Negative
  //   1. Carry
  //   ALU Flags
  //   2. Zero
  //   0. Overflow
endmodule

module Extend (
  input  [23:0] Input,
  input  [1:0] ImmSrc,
  output [31:0] Output
);

  wire [31:0] bit_extender_1_out, bit_extender_2_out, bit_extender_3_out, bit_extender_4_out;

  assign bit_extender_1_out = {{24{1'b0}}, Input[7:0]};  // Bit_Extender bit_extender_1
  assign bit_extender_2_out = {{20{1'b0}}, Input[11:0]};  // Bit_Extender bit_extender_2
  assign bit_extender_3_out = {{8{Input[23]}}, Input};  // Bit_Extender bit_extender_3
  assign bit_extender_4_out = {{27{Input[11]}}, Input[11:7]};  // Bit_Extender bit_extender_4
  Multiplexer #(.select(2), .width(32), .enable("false")) multiplexer_1 (
    .in0(bit_extender_1_out), .in1(bit_extender_2_out), .in2(bit_extender_3_out), .in3(bit_extender_4_out),
    .out(Output), .sel(ImmSrc));

  // Notes on the sheet:
  //   Arithmetic commands
  //   Load
  //   Branch
  //   Logical and arithmetic shifts
endmodule

module Shifter (
  input  [31:0] Input,
  input  [1:0] ShiftType,
  input  [4:0] Shift_Extent,
  output [31:0] Output
);

  wire [31:0] shifter_1_out, shifter_2_out, shifter_3_out, shifter_4_out;

  Shifter_part #(.width(32)) shifter_1 (.in(Input), .\dist (Shift_Extent), .out(shifter_1_out));
  Shifter_part #(.width(32), .shift("lr")) shifter_2 (.in(Input), .\dist (Shift_Extent), .out(shifter_2_out));
  Shifter_part #(.width(32), .shift("ar")) shifter_3 (.in(Input), .\dist (Shift_Extent), .out(shifter_3_out));
  Shifter_part #(.width(32), .shift("rr")) shifter_4 (.in(Input), .\dist (Shift_Extent), .out(shifter_4_out));
  Multiplexer #(.select(2), .width(32), .enable("false")) multiplexer_1 (
    .in0(shifter_1_out), .in1(shifter_2_out), .in2(shifter_3_out), .in3(shifter_4_out), .out(Output),
    .sel(ShiftType));

  // Notes on the sheet:
  //   LSL
  //   LSR
  //   ASR
  //   ROR
endmodule

module Control_unit (
  input  [1:0] Opt,
  input  CLK,
  input  [3:0] Cond,
  input  [2:0] Shift,
  input  [3:0] Rd,
  input  [3:0] Flags,
  input  [5:0] Funct,
  output MemtoReg,
  output [2:0] out_9,
  output [2:0] RegSrc,
  output PCSrc,
  output Move,
  output MemWrite,
  output ALUSrc,
  output RegWrite,
  output [1:0] ImmSrc
);

  wire ALUOp, and_3_out, and_4_out, and_5_out, and_6_out, and_7_out, and_8_out, and_11_out, and_12_out,
       and_13_out, and_14_out, and_19_out, and_20_out, and_21_out, and_22_out, and_23_out, and_24_out,
       and_26_out, and_27_out, and_28_out, and_29_out, and_30_out, and_31_out, CondMet, DiscardResult,
       not_1_out, not_2_out, not_3_out, not_4_out, not_5_out, not_6_out, not_7_out, not_8_out, not_9_out,
       not_10_out, not_11_out, not_12_out, not_13_out, not_14_out, not_15_out, not_16_out, not_17_out,
       not_18_out, not_19_out, not_20_out, not_21_out, not_22_out, not_23_out, or_1_out, or_3_out, or_4_out,
       or_5_out, or_6_out, xnor_1_out;
  wire [0:0] and_15_out;
  wire [1:0] FlagW, multiplexer_8_out, VC_q, ZN_q;
  wire [2:0] multiplexer_1_out, multiplexer_2_out, multiplexer_3_out, multiplexer_4_out;

  not not_1 (not_1_out, Opt[0]);
  not not_2 (not_2_out, Opt[1]);
  and and_1 (ALUOp, not_1_out, not_2_out);
  not not_3 (not_3_out, Funct[3]);
  and and_2 (DiscardResult, not_3_out, Funct[4]);
  Multiplexer #(.select(2), .width(3), .enable("false")) multiplexer_1 (
    .in0(3'b100), .in1(3'b101), .in2(3'b110), .out(multiplexer_1_out), .sel(Shift[2:1]));  // open: in3
  Multiplexer #(.width(3), .enable("false")) multiplexer_2 (
    .in0(multiplexer_1_out), .in1(3'b100), .out(multiplexer_2_out), .sel(Funct[5]));
  Multiplexer #(.select(4), .width(3), .enable("false")) multiplexer_3 (
    .in0(3'b010), .in2(3'b001), .in4(3'b000), .in6(3'b010), .in8(3'b001), .in10(3'b000), .in12(3'b011),
    .in13(multiplexer_2_out), .in15(3'b111), .out(multiplexer_3_out), .sel(Funct[4:1]));  // open: in1, in3, in5, in7, in9, in11, in14
  Multiplexer #(.width(3), .enable("false")) multiplexer_4 (
    .in0(3'b001), .in1(3'b000), .out(multiplexer_4_out), .sel(Funct[3]));
  Multiplexer #(.select(2), .width(3), .enable("false")) multiplexer_5 (
    .in0(multiplexer_3_out), .in1(multiplexer_4_out), .in2(3'b000), .out(out_9), .sel(Opt));  // open: in3
  and and_3 (and_3_out, ~out_9[0], ~out_9[1], ~out_9[2]);  // AND_Gate
  and and_4 (and_4_out, out_9[0], ~out_9[1], ~out_9[2]);  // AND_Gate
  not not_4 (not_4_out, Opt[1]);
  and and_5 (and_5_out, Opt[0], not_5_out);
  not not_5 (not_5_out, Opt[1]);
  not not_6 (not_6_out, Opt[0]);
  not not_7 (not_7_out, Funct[2]);
  not not_8 (not_8_out, Opt[0]);
  not not_9 (not_9_out, Shift[0]);
  and and_6 (and_6_out, Opt[0], ~Opt[1]);  // AND_Gate
  or or_1 (or_1_out, and_3_out, and_4_out);
  not not_10 (not_10_out, Funct[2]);
  Multiplexer #(.width(2), .enable("false")) multiplexer_6 (.in0(Opt), .in1(2'b11), .out(ImmSrc), .sel(and_7_out));
  and and_7 (and_7_out, RegSrc[2], not_11_out);
  not not_11 (not_11_out, Funct[5]);
  and and_8 (and_8_out, Opt[0], not_4_out);
  and and_9 (RegSrc[0], and_5_out, Funct[5]);
  and and_10 (RegSrc[1], not_6_out, Opt[1]);
  not not_12 (not_12_out, Opt[1]);
  and and_11 (and_11_out, RegSrc[2], not_9_out);
  and and_12 (and_12_out, Funct[1], not_10_out, Funct[3], Funct[4]);
  and and_13 (and_13_out, Funct[1], not_7_out, Funct[3], Funct[4]);
  and and_14 (and_14_out, not_8_out, not_12_out);
  or or_2 (ALUSrc, Funct[5], and_11_out, and_6_out);
  and and_15 (and_15_out[0], Funct[0], or_1_out);
  and and_16 (RegSrc[2], ALUOp, and_12_out);
  and and_17 (MemtoReg, Funct[0], and_8_out);
  and and_18 (Move, and_13_out, and_14_out, Funct[5]);
  Multiplexer #(.width(2), .enable("false")) multiplexer_7 (
    .in0(2'b00), .in1({Funct[0], and_15_out[0]}), .out(FlagW), .sel(ALUOp));
  Multiplexer #(.width(2), .enable("false")) multiplexer_8 (
    .in0(2'b00), .in1(FlagW), .out(multiplexer_8_out), .sel(CondMet));
  Register #(.width(2)) VC (.D({Flags[0], Flags[1]}), .en(multiplexer_8_out[1]), .Q(VC_q), .clk(CLK));  // open: clr
  not not_13 (not_13_out, VC_q[1]);
  not not_14 (not_14_out, Opt[0]);
  not not_15 (not_15_out, Opt[1]);
  not not_16 (not_16_out, Opt[1]);
  Register #(.width(2)) ZN (.D({Flags[2], Flags[3]}), .en(multiplexer_8_out[0]), .Q(ZN_q), .clk(CLK));  // open: clr
  not not_17 (not_17_out, ZN_q[1]);
  not not_18 (not_18_out, VC_q[0]);
  and and_19 (and_19_out, not_14_out, not_15_out);
  not not_19 (not_19_out, DiscardResult);
  not not_20 (not_20_out, ZN_q[0]);
  and and_20 (and_20_out, and_19_out, not_19_out);
  and and_21 (and_21_out, Opt[0], not_16_out);
  and and_22 (and_22_out, VC_q[0], not_17_out);
  or or_3 (or_3_out, not_18_out, ZN_q[1]);
  and and_23 (and_23_out, Funct[0], and_21_out);
  xnor xnor_1 (xnor_1_out, ZN_q[0], VC_q[1]);
  or or_4 (or_4_out, and_20_out, and_23_out);
  not not_21 (not_21_out, xnor_1_out);
  and and_24 (and_24_out, xnor_1_out, not_17_out);
  or or_5 (or_5_out, not_21_out, ZN_q[1]);
  and and_25 (RegWrite, CondMet, or_4_out);
  Multiplexer #(.select(4), .enable("false")) multiplexer_9 (
    .in0(ZN_q[1]), .in1(not_17_out), .in2(VC_q[0]), .in3(not_18_out), .in4(ZN_q[0]), .in5(not_20_out),
    .in6(VC_q[1]), .in7(not_13_out), .in8(and_22_out), .in9(or_3_out), .in10(xnor_1_out), .in11(not_21_out),
    .in12(and_24_out), .in13(or_5_out), .in14(1'b1), .out(CondMet), .sel(Cond));  // open: in15
  not not_22 (not_22_out, Opt[1]);
  and and_26 (and_26_out, Rd[0], Rd[1], Rd[3]);
  and and_27 (and_27_out, ~Opt[0], Opt[1]);  // AND_Gate
  and and_28 (and_28_out, Opt[0], not_22_out);
  and and_29 (and_29_out, and_26_out, RegWrite);
  not not_23 (not_23_out, Funct[0]);
  and and_30 (and_30_out, not_23_out, and_28_out);
  or or_6 (or_6_out, and_29_out, and_27_out);
  and and_31 (and_31_out, or_6_out, CondMet);
  and and_32 (MemWrite, and_30_out, CondMet);
  not not_24 (PCSrc, and_31_out);

  // Other names for the same wires on the sheet: L = Funct[0]; S = Funct[0]; C = Flags[1]; V = Flags[0]; N = Flags[3];
  //   Z = Flags[2]; ALUControl[2:0] = out_9; CMD[3:0] = Funct[4:1]; W = Funct[1]; B = Funct[2]; U = Funct[3];
  //   P = Funct[4]; I = Funct[5]; IsShift = RegSrc[2]

  // Notes on the sheet:
  //   ADD
  //   AND
  //   SUB
  //   ALU supported data processing instructions
  //   ORR
  //   LSL
  //   LSR
  //   NOT
  //   ASR
  //   Immediate Bit
  //   Load:1, Store:0
  //   flags set bit on arithmetic commands
  //   Adding offset:1, subtracting offset:0
  //   Tunnels for various inputs to the Control Unit
  //   Check for add or sub
  //   Signal is set when the operand is shift instruction
  //   Extender logic for various instructions
  //   MemToReg signal is 1 when there is a ldr instruction
  //   OPT = 01 for load/store instructions in ARM
  //   XX                       Y
  //   01 if branch
  //   10 if shift
  //   00 else
  //   ALUSrc signal chooses from register operand or immediate
  //   01: Zero-Extend Immediate for ldr instruction
  //   10: Sign-Extend immediate for branch instruction
  //   11: Zero-Extend 5 bits for shift instruction
  //   1 if str
  //   Move instruction to put immediate into register file
  //   00: Zero-Extend Immediate for Arithmetic and logical commands
  //   Decoder
  //   0 if arith. command without Imm.
  //   Conditional Logic
  //   OPT=0 && Result not discarded
  //   OPT=01 && L=1 for ldr instruction
  //   Logic for writing to register file
  //   1 if condition is true
  //   Whether PC picks from branch or next instr in ROM
  //   Memory write signal true in case of store instruction
endmodule
